# Fritzing sketch Project Fritzig File (saved by Fritzing 0.9.3b)

parts:
  Part1 = Arduino Uno (Rev3)
  U1 = POT [package=pot_alpha_rv16af-20]
  LCD1 = LCD screen
  M1 = fc-51 [package=THT]
  M2 = fc-51 [package=THT]
  Mod1 = Passive Buzzer

nets:
  N1: Part1.A4/SDA, M2.pin1
  N2: Part1.A5/SCL, M1.pin1
  N3: Part1.D11_PWM/MOSI, LCD1.E
  N4: Part1.D12/MISO, LCD1.RS
  GND: Part1.GND, LCD1.VSS
  N5: Part1.D0/RX, Mod1.S
  N6: Part1.D2, LCD1.DB7
  N7: Part1.D3_PWM, LCD1.DB6
  N8: Part1.D4, LCD1.DB5
  N9: Part1.D5_PWM, LCD1.DB4
  5V: Part1.5V, LCD1.VDD
  N10: U1.S, LCD1.V0

notes:
  IR Sensor & Receiver 1
  IR Sensor & Receiver 2
  Buzzer
  LCD Display
  Potentiometer
  Arduino UNO
  Legend:
  Red = Live VCC
  Black = Neutral GND
  Cyan = LCD Display
  Green = Buzzer
  Grey = Potentiometer
  Blue = IR Sensors
